# Fritzing sketch Untitled Sketch (saved by Fritzing 0.9.3b)

parts:
  Part1 = Arduino Uno (Rev3) - ICSP
  IC1 = L293D [package=THT]
  M1 = DC Motor  # not connected
  M2 = DC Motor  # not connected
  VCC1 = Battery block 9V

nets:
  N1: Part1.A4/SDA, IC1.In_4
  N2: Part1.D8, IC1.In_3
  N3: Part1.GND, IC1.0V, VCC1.-
  N4: Part1.D4, IC1.In_1
  N5: Part1.D5_PWM, IC1.Enable_2
  N6: Part1.D6_PWM, IC1.Enable_1
  N7: Part1.D7, IC1.In_2
  N8: Part1.5V, IC1.+V

notes:
  LEFT MOTOR
  RIGHT MOTOR
  6IR ARRAY SENSOR
